# Fritzing sketch LedMatrix2 (saved by Fritzing 0.9.3b)
breadboards: 1

parts:
  U1 = 74HC595 [package="DIP16 [THT]"]
  U2 = 74HC595 [package="DIP16 [THT]"]
  module2 = 788BS Dot matix
  Mod1 = Raspberry Pi Pico

nets:
  N1: U1.Q1, module2.P6
  N2: U1.Q2, module2.P5
  N3: U1.Q3, module2.P10
  N4: U1.Q4, module2.P3
  N5: U1.Q5, module2.P11
  N6: U1.Q6, module2.P15
  N7: U1.Q7, module2.P16
  GND: U1.GND, U2.GND, Mod1.pin_5, Mod1.pin_111, Mod1.pin_112
  VCC: U1.MR, U1.VCC, U2.MR, U2.VCC, Mod1.pin_39, Mod1.pin_44
  N8: U1.SH_CP, U2.SH_CP, Mod1.pin_26, Mod1.pin_69, Mod1.pin_70
  N9: U1.ST_CP, U2.ST_CP, Mod1.pin_25, Mod1.pin_71, Mod1.pin_72
  N10: U1.OE, U2.OE, Mod1.pin_3, Mod1.pin_8, Mod1.pin_13, Mod1.pin_18, Mod1.pin_23, Mod1.pin_28, Mod1.pin_33, Mod1.pin_38, Mod1.pin_42, Mod1.pin_45, Mod1.pin_46, Mod1.pin_55, Mod1.pin_56, Mod1.pin_65, Mod1.pin_66, Mod1.pin_75, Mod1.pin_76, Mod1.pin_85, Mod1.pin_86, Mod1.pin_95, Mod1.pin_96, Mod1.pin_105, Mod1.pin_106, Mod1.pin_115, Mod1.pin_116
  N11: U1.DS, U2.Q7'
  N12: U1.Q0, module2.P13
  N13: U2.Q1, module2.P14
  N14: U2.Q2, module2.P1
  N15: U2.Q3, module2.P12
  N16: U2.Q4, module2.P8
  N17: U2.Q5, module2.P2
  N18: U2.Q6, module2.P7
  N19: U2.Q7, module2.P4
  N20: U2.DS, Mod1.pin_24, Mod1.pin_73, Mod1.pin_74
  N21: U2.Q0, module2.P9
  N22: Mod1.pin_1, Mod1.pin_119, Mod1.pin_120
  N23: Mod1.pin_2, Mod1.pin_117, Mod1.pin_118
  N24: Mod1.pin_4, Mod1.pin_113, Mod1.pin_114
  N25: Mod1.pin_6, Mod1.pin_109, Mod1.pin_110
  N26: Mod1.pin_7, Mod1.pin_107, Mod1.pin_108
  N27: Mod1.pin_9, Mod1.pin_103, Mod1.pin_104
  N28: Mod1.pin_10, Mod1.pin_101, Mod1.pin_102
  N29: Mod1.pin_11, Mod1.pin_99, Mod1.pin_100
  N30: Mod1.pin_12, Mod1.pin_97, Mod1.pin_98
  N31: Mod1.pin_14, Mod1.pin_93, Mod1.pin_94
  N32: Mod1.pin_15, Mod1.pin_91, Mod1.pin_92
  N33: Mod1.pin_16, Mod1.pin_89, Mod1.pin_90
  N34: Mod1.pin_17, Mod1.pin_87, Mod1.pin_88
  N35: Mod1.pin_19, Mod1.pin_83, Mod1.pin_84
  N36: Mod1.pin_20, Mod1.pin_81, Mod1.pin_82
  N37: Mod1.pin_21, Mod1.pin_79, Mod1.pin_80
  N38: Mod1.pin_22, Mod1.pin_77, Mod1.pin_78
  N39: Mod1.pin_27, Mod1.pin_67, Mod1.pin_68
  N40: Mod1.pin_29, Mod1.pin_63, Mod1.pin_64
  N41: Mod1.pin_30, Mod1.pin_61, Mod1.pin_62
  N42: Mod1.pin_31, Mod1.pin_59, Mod1.pin_60
  N43: Mod1.pin_32, Mod1.pin_57, Mod1.pin_58
  N44: Mod1.pin_34, Mod1.pin_53, Mod1.pin_54
  N45: Mod1.pin_35, Mod1.pin_51, Mod1.pin_52
  N46: Mod1.pin_36, Mod1.pin_49, Mod1.pin_50
  N47: Mod1.pin_37, Mod1.pin_47, Mod1.pin_48

custom parts:
  788BS Dot matix: 788BS 8x8 dot matix from SunFounder
  Raspberry Pi Pico: Raspberry Pi Pico. Based around the RP2040 microcontroller the Pico is a low cost microcontroller device bringing Raspberry Pi quality, cost, and easy of use to the microcontroller space. Jan 2021, Split part in to two versions: tht (this one) and SMD. This one will drill holes for a .1 in header in pcb to allow plugging in the module as well as providing pads to solder the module to the top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
