# Fritzing sketch stepper motor (saved by Fritzing 0.9.3b)
breadboards: 1

parts:
  Mod2 = Raspberry Pi Pico
  IC2 = Power Module V1.0 [package=THT]
  S1 = Pushbutton [package="[THT]"]
  S2 = Pushbutton [package="[THT]"]
  R1 = Resistor [tolerance=±5% resistance=10k package=THT]
  U1 = Stepper Motor Driver-v1.0 [package="DIP28 [THT]"]
  module1 = Step Motor

nets:
  N1: Mod2.pin_1, Mod2.pin_119, Mod2.pin_120
  N2: Mod2.pin_2, Mod2.pin_117, Mod2.pin_118
  N3: Mod2.pin_3, Mod2.pin_8, Mod2.pin_13, Mod2.pin_18, Mod2.pin_23, Mod2.pin_28, Mod2.pin_33, Mod2.pin_38, Mod2.pin_42, Mod2.pin_45, Mod2.pin_46, Mod2.pin_55, Mod2.pin_56, Mod2.pin_65, Mod2.pin_66, Mod2.pin_75, Mod2.pin_76, Mod2.pin_85, Mod2.pin_86, Mod2.pin_95, Mod2.pin_96, Mod2.pin_105, Mod2.pin_106, Mod2.pin_115, Mod2.pin_116, IC2.3.3V, IC2.-#4, S1.Pin_1, S1.Pin_2
  N4: Mod2.pin_4, Mod2.pin_113, Mod2.pin_114
  N5: Mod2.pin_5, Mod2.pin_111, Mod2.pin_112
  N6: Mod2.pin_6, Mod2.pin_109, Mod2.pin_110
  N7: Mod2.pin_7, Mod2.pin_107, Mod2.pin_108
  N8: Mod2.pin_9, Mod2.pin_103, Mod2.pin_104
  N9: Mod2.pin_10, Mod2.pin_101, Mod2.pin_102
  N10: Mod2.pin_11, Mod2.pin_99, Mod2.pin_100
  N11: Mod2.pin_12, Mod2.pin_97, Mod2.pin_98
  N12: Mod2.pin_14, Mod2.pin_93, Mod2.pin_94
  N13: Mod2.pin_15, Mod2.pin_91, Mod2.pin_92
  N14: Mod2.pin_16, Mod2.pin_89, Mod2.pin_90
  N15: Mod2.pin_17, Mod2.pin_87, Mod2.pin_88
  N16: Mod2.pin_19, Mod2.pin_83, Mod2.pin_84, S2.Pin_3, S2.Pin_4, R1.Pin_1
  N17: Mod2.pin_20, Mod2.pin_81, Mod2.pin_82
  N18: Mod2.pin_21, Mod2.pin_79, Mod2.pin_80
  N19: Mod2.pin_22, Mod2.pin_77, Mod2.pin_78
  N20: Mod2.pin_24, Mod2.pin_73, Mod2.pin_74, U1.IN4
  N21: Mod2.pin_25, Mod2.pin_71, Mod2.pin_72, U1.IN3
  N22: Mod2.pin_26, Mod2.pin_69, Mod2.pin_70, U1.IN2
  N23: Mod2.pin_27, Mod2.pin_67, Mod2.pin_68, U1.IN1
  N24: Mod2.pin_29, Mod2.pin_63, Mod2.pin_64
  N25: Mod2.pin_30, Mod2.pin_61, Mod2.pin_62, S1.Pin_3, S1.Pin_4
  N26: Mod2.pin_31, Mod2.pin_59, Mod2.pin_60
  N27: Mod2.pin_32, Mod2.pin_57, Mod2.pin_58
  N28: Mod2.pin_34, Mod2.pin_53, Mod2.pin_54
  N29: Mod2.pin_35, Mod2.pin_51, Mod2.pin_52
  N30: Mod2.pin_36, Mod2.pin_49, Mod2.pin_50
  N31: Mod2.pin_37, Mod2.pin_47, Mod2.pin_48
  N32: Mod2.pin_39, Mod2.pin_44
  N33: IC2.+#2, IC2.GND, S2.Pin_1, S2.Pin_2
  N34: IC2.+#3, U1.+
  N35: IC2.-#5, R1.Pin_0, U1.-
  N36: U1.OUT1, module1.blue
  N37: U1.OUT2, module1.pink
  N38: U1.OUT3, module1.red
  N39: U1.OUT4, module1.orange
  N40: U1.COM, module1.yellow

custom parts:
  Raspberry Pi Pico: Raspberry Pi Pico. Based around the RP2040 microcontroller the Pico is a low cost microcontroller device bringing Raspberry Pi quality, cost, and easy of use to the microcontroller space. Jan 2021, Split part in to two versions: tht (this one) and SMD. This one will drill holes for a .1 in header in pcb to allow plugging in the module as well as providing pads to solder the module to the top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
  Power Module V1.0: Power Module used for BreadBoard www.sunfounder.com
  Pushbutton: A generic pushbutton.
  Stepper Motor Driver-v1.0: Stepper Motor Driver
  Step Motor: step motor
